# Fritzing sketch P2 (saved by Fritzing 0.9.3b)
breadboards: 1

parts:
  R1 = Resistor [tolerance=±5% resistance=220 package=THT]
  V1 = DC Power [voltage=5]

nets:
  N1: R1.Pin_0, V1.V+
  GND: R1.Pin_1, V1.V-
